// Logisim project 16 bit ALU.circ as structural Verilog: 1 circuit, main circuit main
// 16 bit ALU
module main (
  input  [15:0] B,
  input  [15:0] A,
  input  Cin,
  input  A_invert,
  input  B_invert,
  input  [2:0] Operation,
  output [15:0] out_7,
  output Cout,
  output BEQ
);

  wire main_1_cout, main_2_cout, main_3_cout, or_1_out;

  _4_bit_alu_main main_1 (
    .A_invert(A_invert), .B_invert(B_invert), .A0(A[0]), .A1(A[1]), .A2(A[2]), .A3(A[3]), .B0(B[0]),
    .B1(B[1]), .B2(B[2]), .B3(B[3]), .Cin(Cin), .Operation(Operation), .S0(out_7[0]), .S1(out_7[1]),
    .S2(out_7[2]), .S3(out_7[3]), .Cout(main_1_cout));
  _4_bit_alu_main main_2 (
    .A_invert(A_invert), .B_invert(B_invert), .A0(A[4]), .A1(A[5]), .A2(A[6]), .A3(A[7]), .B0(B[4]),
    .B1(B[5]), .B2(B[6]), .B3(B[7]), .Cin(main_1_cout), .Operation(Operation), .S0(out_7[4]), .S1(out_7[5]),
    .S2(out_7[6]), .S3(out_7[7]), .Cout(main_2_cout));
  _4_bit_alu_main main_3 (
    .A_invert(A_invert), .B_invert(B_invert), .A0(A[8]), .A1(A[9]), .A2(A[10]), .A3(A[11]), .B0(B[8]),
    .B1(B[9]), .B2(B[10]), .B3(B[11]), .Cin(main_2_cout), .Operation(Operation), .S0(out_7[8]),
    .S1(out_7[9]), .S2(out_7[10]), .S3(out_7[11]), .Cout(main_3_cout));
  _4_bit_alu_main main_4 (
    .A_invert(A_invert), .B_invert(B_invert), .A0(A[12]), .A1(A[13]), .A2(A[14]), .A3(A[15]), .B0(B[12]),
    .B1(B[13]), .B2(B[14]), .B3(B[15]), .Cin(main_3_cout), .Operation(Operation), .S0(out_7[12]),
    .S1(out_7[13]), .S2(out_7[14]), .S3(out_7[15]), .Cout(Cout));
  or or_1 (or_1_out, out_7[0], out_7[15], out_7[1], out_7[2], out_7[3], out_7[4], out_7[5], out_7[6], out_7[7], out_7[8], out_7[9], out_7[10], out_7[11], out_7[12], out_7[13], out_7[14]);
  not not_1 (BEQ, or_1_out);

  // Notes on the sheet:
  //   Result
endmodule
