// Logisim project 16 bit alu demo.circ as structural Verilog: 1 circuit, main circuit main
module main (
  input  A_invert,
  input  B_invert,
  input  [3:0] in_3,
  input  in_4,
  input  [3:0] in_5,
  input  [3:0] in_6,
  input  [1:0] Operation,
  output [15:0] Result,
  output Zero,
  output Cout
);

  wire clock_1_out;
  wire [15:0] main_1_register_1_data, main_1_register_2_data;

  Clock clock_1 (.out(clock_1_out));
  Register_file_main main_1 (
    .Data(Result), .Register_1_Data(main_1_register_1_data), .Register_2_Data(main_1_register_2_data),
    .Write_Register(in_3), .Read_Register_1(in_5), .Read_Register_2(in_6), .CLK(clock_1_out));  // open: Write_register_2
  // _16_bit_ALU_main main_2: pin names not known; wires that end beside it: main_1_register_1_data, main_1_register_2_data, in_4, A_invert, Operation, Cout, B_invert, Result, Zero

  // Notes on the sheet:
  //   10 Or
  //   00 - Add
  //   00 - Sub/bne (B invert - 1)
  //   01 And
  //   11 Nor
endmodule
