// Logisim project 4 bit alu.circ as structural Verilog: 1 circuit, main circuit main
module main (
  input  A_invert,
  input  B_invert,
  input  A0,
  input  A1,
  input  A2,
  input  A3,
  input  B0,
  input  B1,
  input  B2,
  input  B3,
  input  Cin,
  input  [2:0] Operation,
  output S0,
  output S1,
  output S2,
  output S3,
  output Cout
);

  wire A0_B0_out, A0_nor_B0_out, A0_XOR_B0_out, A0B0_out, A1_B1__prime_out, A1_B1_out, A1B1_out,
       A2_B2__prime_out, A2_B2_out, A2B2_out, A3_B3__prime_out, A3_B3_out, A3B3_out, main_1_s0, main_1_s1,
       main_1_s2, main_1_s3, multiplexer_1_out, multiplexer_2_out, multiplexer_3_out, multiplexer_4_out,
       multiplexer_5_out, multiplexer_6_out, multiplexer_7_out, multiplexer_8_out, not_1_out, not_2_out,
       not_3_out, not_4_out, not_5_out, not_6_out, not_7_out, not_8_out, xor_1_out, xor_2_out, xor_3_out;

  Multiplexer multiplexer_1 (.in0(A0), .in1(not_1_out), .out(multiplexer_1_out), .sel(A_invert));  // open: en
  not not_1 (not_1_out, A0);
  Multiplexer multiplexer_2 (.in0(A1), .in1(not_2_out), .out(multiplexer_2_out), .sel(A_invert));  // open: en
  not not_2 (not_2_out, A1);
  Multiplexer multiplexer_3 (.in0(A2), .in1(not_3_out), .out(multiplexer_3_out), .sel(A_invert));  // open: en
  not not_3 (not_3_out, A2);
  Multiplexer multiplexer_4 (.in0(A3), .in1(not_4_out), .out(multiplexer_4_out), .sel(A_invert));  // open: en
  not not_4 (not_4_out, A3);
  Multiplexer multiplexer_5 (.in0(B0), .in1(not_5_out), .out(multiplexer_5_out), .sel(B_invert));  // open: en
  not not_5 (not_5_out, B0);
  Multiplexer multiplexer_6 (.in0(B1), .in1(not_6_out), .out(multiplexer_6_out), .sel(B_invert));  // open: en
  not not_6 (not_6_out, B1);
  Multiplexer multiplexer_7 (.in0(B2), .in1(not_7_out), .out(multiplexer_7_out), .sel(B_invert));  // open: en
  not not_7 (not_7_out, B2);
  Multiplexer multiplexer_8 (.in0(B3), .in1(not_8_out), .out(multiplexer_8_out), .sel(B_invert));  // open: en
  not not_8 (not_8_out, B3);
  _4_bit_carry_look_ahead_adder_main main_1 (
    .A0(multiplexer_1_out), .A1(multiplexer_2_out), .A2(multiplexer_3_out), .A3(multiplexer_4_out),
    .B0(multiplexer_5_out), .B1(multiplexer_6_out), .B2(multiplexer_7_out), .B3(multiplexer_8_out),
    .Cin(Cin), .S0(main_1_s0), .S1(main_1_s1), .S2(main_1_s2), .S3(main_1_s3), .Cout(Cout));
  and A0B0 (A0B0_out, A0, B0);
  or A0_B0 (A0_B0_out, A0, B0);
  nor A0_nor_B0 (A0_nor_B0_out, A0, B0);
  and A1B1 (A1B1_out, A1, B1);
  or A1_B1 (A1_B1_out, A1, B1);
  nor A1_B1__prime (A1_B1__prime_out, A1, B1);
  and A2B2 (A2B2_out, A2, B2);
  or A2_B2 (A2_B2_out, A2, B2);
  nor A2_B2__prime (A2_B2__prime_out, A2, B2);
  and A3B3 (A3B3_out, A3, B3);
  or A3_B3 (A3_B3_out, A3, B3);
  nor A3_B3__prime (A3_B3__prime_out, A3, B3);
  xor xor_1 (xor_1_out, A3, B3);
  xor A0_XOR_B0 (A0_XOR_B0_out, A0, B0);
  xor xor_2 (xor_2_out, A1, B1);
  xor xor_3 (xor_3_out, A2, B2);
  Multiplexer #(.select(3)) multiplexer_9 (
    .in0(main_1_s2), .in1(A2B2_out), .in2(A2_B2_out), .in3(A2_B2__prime_out), .in4(xor_3_out), .out(S2),
    .sel(Operation));  // open: in5, in6, in7, en
  Multiplexer #(.select(3)) multiplexer_10 (
    .in0(main_1_s3), .in1(A3B3_out), .in2(A3_B3_out), .in3(A3_B3__prime_out), .in4(xor_1_out), .out(S3),
    .sel(Operation));  // open: in5, in6, in7, en
  Multiplexer #(.select(3)) multiplexer_11 (
    .in0(main_1_s0), .in1(A0B0_out), .in2(A0_B0_out), .in3(A0_nor_B0_out), .in4(A0_XOR_B0_out), .out(S0),
    .sel(Operation));  // open: in5, in6, in7, en
  Multiplexer #(.select(3)) multiplexer_12 (
    .in0(main_1_s1), .in1(A1B1_out), .in2(A1_B1_out), .in3(A1_B1__prime_out), .in4(xor_2_out), .out(S1),
    .sel(Operation));  // open: in5, in6, in7, en
endmodule
