// Logisim project 4 bit carry look ahead adder.circ as structural Verilog: 1 circuit, main circuit main
module main (
  input  A0,
  input  A1,
  input  A2,
  input  A3,
  input  B0,
  input  B1,
  input  B2,
  input  B3,
  input  Cin,
  output S0,
  output S1,
  output S2,
  output S3,
  output Cout
);

  wire main_1_c1, main_2_c2, main_3_c3, xor_1_out, xor_2_out, xor_3_out, xor_4_out;

  xor xor_1 (xor_1_out, A0, B0);
  xor xor_2 (xor_2_out, A1, B1);
  xor xor_3 (xor_3_out, A2, B2);
  xor xor_4 (xor_4_out, A3, B3);
  xor xor_5 (S0, xor_1_out, Cin);
  c1_main main_1 (.A0(A0), .B0(B0), .Cin(Cin), .C1(main_1_c1));
  c2_main main_2 (.C2(main_2_c2), .A0(A0), .A1(A1), .B0(B0), .B1(B1), .Cin(Cin));
  c3_main main_3 (.C3(main_3_c3), .A0(A0), .A1(A1), .A2(A2), .B0(B0), .B1(B1), .B2(B2), .Cin(Cin));
  c4_main main_4 (.C4(Cout), .A0(A0), .A1(A1), .A2(A2), .A3(A3), .B0(B0), .B1(B1), .B2(B2), .B3(B3), .Cin(Cin));
  xor xor_6 (S1, main_1_c1, xor_2_out);
  xor xor_7 (S2, xor_3_out, main_2_c2);
  xor xor_8 (S3, xor_4_out, main_3_c3);
endmodule
