// Logisim project c1.circ as structural Verilog: 1 circuit, main circuit main
module main (
  input  A0,
  input  B0,
  input  Cin,
  output C1
);

  wire and_1_out, and_2_out, or_1_out;

  and and_1 (and_1_out, B0, A0);
  or or_1 (or_1_out, A0, B0);
  and and_2 (and_2_out, or_1_out, Cin);
  or or_2 (C1, and_1_out, and_2_out);

  // Notes on the sheet:
  //   AB
  //   A+B
  //   (A+B)Cin
endmodule
