// Logisim project c2.circ as structural Verilog: 1 circuit, main circuit main
module main (
  input  A0,
  input  A1,
  input  B0,
  input  B1,
  input  Cin,
  output C2
);

  wire and_1_out, and_2_out, and_3_out, and_4_out, or_1_out, or_2_out, or_3_out;

  and and_1 (and_1_out, A1, B1);
  or or_1 (or_1_out, A1, B1);
  and and_2 (and_2_out, A0, B0);
  or or_2 (or_2_out, A1, B1);
  or or_3 (or_3_out, A0, B0);
  and and_3 (and_3_out, or_1_out, and_2_out);
  and and_4 (and_4_out, or_2_out, or_3_out, Cin);
  or or_4 (C2, and_1_out, and_3_out, and_4_out);

  // Notes on the sheet:
  //   A1B1
  //   A1+B1
  //   A0B0
endmodule
