// Logisim project c4.circ as structural Verilog: 1 circuit, main circuit main
module main (
  input  A0,
  input  A1,
  input  A2,
  input  A3,
  input  B0,
  input  B1,
  input  B2,
  input  B3,
  input  Cin,
  output C4
);

  wire A0_B0_out, A0B0_out, A1_B1_out, A1B1_out, A2_B2_out, A2B2_out, A3_B3_out, A3B3_out, and_1_out,
       and_2_out, and_3_out, and_4_out;

  and A3B3 (A3B3_out, B3, A3);
  or A3_B3 (A3_B3_out, A3, B3);
  and A2B2 (A2B2_out, A2, B2);
  or A2_B2 (A2_B2_out, A2, B2);
  and A1B1 (A1B1_out, A1, B1);
  or A1_B1 (A1_B1_out, A1, B1);
  and A0B0 (A0B0_out, A0, B0);
  or A0_B0 (A0_B0_out, A0, B0);
  and and_1 (and_1_out, A3_B3_out, A2B2_out);
  and and_2 (and_2_out, A3_B3_out, A2_B2_out, A1B1_out);
  and and_3 (and_3_out, A3_B3_out, A2_B2_out, A1_B1_out, A0B0_out);
  and and_4 (and_4_out, A3_B3_out, A2_B2_out, A1_B1_out, A0_B0_out, Cin);
  or or_1 (C4, A3B3_out, and_1_out, and_2_out, and_3_out, and_4_out);
endmodule
