// Logisim project CPU.circ as structural Verilog: 1 circuit, main circuit main
module main (
  input  Jump,
  input  Branch,
  input  in_3,
  input  [2:0] ALUOp,
  output [3:0] out_5
);

  wire and_1_out, clock_1_out, main_1_alusrc, main_1_b_prime_cin, main_1_l_r, main_1_load, main_1_memread,
       main_1_regdst, main_1_regwrite, main_1_shift, main_1_store, main_3_beq;
  wire [3:0] multiplexer_1_out, rom_1_data;
  wire [7:0] adder_1_out, adder_2_out, bit_extender_2_out, bit_extender_3_out, multiplexer_3_out,
       multiplexer_4_out, PC_q;
  wire [11:0] rom_1_data_2;
  wire [15:0] bit_extender_1_out, main_2_register_1_data, main_2_register_2_data, main_3_out_7, main_4_out_4,
       multiplexer_2_out, multiplexer_5_out, multiplexer_6_out, ram_1_data;

  ControlUnit_main main_1 (
    .Opcode(rom_1_data), .RegWrite(main_1_regwrite), .Regdst(main_1_regdst), .AluSrc(main_1_alusrc),
    .MemRead(main_1_memread), .ALUop(ALUOp), .Branch(Branch), .Jump(Jump), .Load(main_1_load),
    .Store(main_1_store), .B_prime_Cin(main_1_b_prime_cin), .L_R(main_1_l_r), .Shift(main_1_shift));
  Register PC (.D(multiplexer_4_out), .Q(PC_q), .clk(clock_1_out));  // open: en, clr
  Clock clock_1 (.out(clock_1_out));
  Adder adder_1 (.a(PC_q), .b(8'h1), .out(adder_1_out));  // open: cin, cout
  ROM #(.dataWidth(16)) rom_1 (.addr(PC_q), .data({rom_1_data, rom_1_data_2}));  // open: sel
  Multiplexer #(.width(4)) multiplexer_1 (
    .in0(rom_1_data_2[3:0]), .in1(rom_1_data_2[7:4]), .out(multiplexer_1_out), .sel(main_1_regdst));  // open: en
  assign bit_extender_1_out = {{12{rom_1_data_2[3]}}, rom_1_data_2[3:0]};  // Bit_Extender bit_extender_1
  Bit_Extender #(.in_width(12), .out_width(8)) bit_extender_2 (.in(rom_1_data_2), .out(bit_extender_2_out));
  Register_file_main main_2 (
    .Data(multiplexer_6_out), .Register_1_Data(main_2_register_1_data),
    .Register_2_Data(main_2_register_2_data), .Write_Register(multiplexer_1_out),
    .Read_Register_1(rom_1_data_2[11:8]), .Read_Register_2(rom_1_data_2[7:4]), .CLK(clock_1_out),
    .Write_register_2(main_1_regwrite));
  Adder adder_2 (.a(adder_1_out), .b(bit_extender_3_out), .out(adder_2_out));  // open: cin, cout
  Bit_Extender #(.in_width(16), .out_width(8)) bit_extender_3 (.in(bit_extender_1_out), .out(bit_extender_3_out));
  Multiplexer #(.width(16)) multiplexer_2 (
    .in0(main_2_register_2_data), .in1(bit_extender_1_out), .out(multiplexer_2_out), .sel(main_1_alusrc));  // open: en
  and and_1 (and_1_out, Branch, main_3_beq);
  _16_bit_ALU_main main_3 (
    .A_invert(in_3), .B_invert(main_1_b_prime_cin), .Operation(ALUOp), .Cin(main_1_b_prime_cin),
    .BEQ(main_3_beq), .out_7(main_3_out_7), .A(main_2_register_1_data), .B(multiplexer_2_out));  // open: Cout
  _16bit_sll_srl_main main_4 (
    .in_1(main_2_register_1_data), .in_2(rom_1_data_2[3:0]), .in_3(main_1_l_r), .out_4(main_4_out_4));
  Multiplexer #(.width(8)) multiplexer_3 (
    .in0(adder_1_out), .in1(adder_2_out), .out(multiplexer_3_out), .sel(and_1_out));  // open: en
  Multiplexer #(.width(8)) multiplexer_4 (
    .in0(multiplexer_3_out), .in1(bit_extender_2_out), .out(multiplexer_4_out), .sel(Jump));  // open: en
  RAM #(.addrWidth(16), .dataWidth(16), .bus("separate")) ram_1 (
    .addr(main_3_out_7), .din(main_2_register_2_data), .data(ram_1_data), .str(main_1_store),
    .clk(clock_1_out), .ld(main_1_load));  // open: sel, clr
  Multiplexer #(.width(16)) multiplexer_5 (
    .in0(main_3_out_7), .in1(ram_1_data), .out(multiplexer_5_out), .sel(main_1_memread));  // open: en
  Multiplexer #(.width(16)) multiplexer_6 (
    .in0(multiplexer_5_out), .in1(main_4_out_4), .out(multiplexer_6_out), .sel(main_1_shift));  // open: en

  // Notes on the sheet:
  //   contents of rom_1 (hex, n*v repeats v):
  //   c154 1328 2129 312a 4125 9264 a274 b284 5393 6652 e236 7131 176 f004
endmodule
