// Logisim project Binverse Cin.circ as structural Verilog: 1 circuit, main circuit main
module main (
  input  [3:0] in_1,
  output out_2
);

  wire and_1_out, and_2_out, not_1_out, not_2_out, not_3_out;

  not not_1 (not_1_out, in_1[2]);
  not not_2 (not_2_out, in_1[1]);
  not not_3 (not_3_out, in_1[3]);
  and and_1 (and_1_out, not_3_out, not_1_out, not_2_out, in_1[0]);
  and and_2 (and_2_out, not_3_out, in_1[2], in_1[1], in_1[0]);
  or or_1 (out_2, and_1_out, and_2_out);
endmodule
