// Logisim project Branch.circ as structural Verilog: 1 circuit, main circuit main
module main (
  input  [3:0] in_1,
  output out_2
);

  wire not_1_out;

  not not_1 (not_1_out, in_1[3]);
  and and_1 (out_2, not_1_out, in_1[2], in_1[1], in_1[0]);
endmodule
