// Logisim project ControlUnit.circ as structural Verilog: 1 circuit, main circuit main
module main (
  input  [3:0] Opcode,
  output RegWrite,
  output Regdst,
  output AluSrc,
  output MemRead,
  output [2:0] ALUop,
  output Branch,
  output Jump,
  output Load,
  output Store,
  output B_prime_Cin,
  output L_R,
  output Shift
);

  RegDst_main main_1 (.in_1(Opcode), .out_2(Regdst));
  ALUsrc_main main_2 (.in_1(Opcode), .out_2(AluSrc));
  MemRead_main main_3 (.in_1(Opcode), .out_2(MemRead));
  ALUop_main main_4 (.in_1(Opcode), .out_2(ALUop));
  Branch_main main_5 (.in_1(Opcode), .out_2(Branch));
  jump_main main_6 (.in_1(Opcode), .out_2(Jump));
  Load_main main_7 (.in_1(Opcode), .out_2(Load));
  Store_main main_8 (.in_1(Opcode), .out_2(Store));
  Binverse_Cin_main main_9 (.in_1(Opcode), .out_2(B_prime_Cin));
  LR_main main_10 (.in_1(Opcode), .out_2(L_R));
  Shift_main main_11 (.in_1(Opcode), .out_2(Shift));
  Write_Register_main main_12 (.Inout(Opcode), .out_2(RegWrite));
endmodule
