// Logisim project Write Register.circ as structural Verilog: 1 circuit, main circuit main
module main (
  input  [3:0] Inout,
  output out_2
);

  wire and_1_out, and_2_out, not_1_out, not_2_out, not_3_out;

  not not_1 (not_1_out, Inout[2]);
  not not_2 (not_2_out, Inout[1]);
  not not_3 (not_3_out, Inout[0]);
  and and_1 (and_1_out, Inout[1], not_1_out);
  and and_2 (and_2_out, Inout[3], Inout[1], not_3_out);
  or or_1 (out_2, and_2_out, and_1_out, not_2_out);
endmodule
