// Logisim project Register file.circ as structural Verilog: 1 circuit, main circuit main
module main (
  input  [3:0] Read_Register_1,
  input  [3:0] Write_Register,
  input  Write_register_2,
  input  [15:0] Data,
  input  CLK,
  input  [3:0] Read_Register_2,
  output [15:0] Register_1_Data,
  output [15:0] Register_2_Data
);

  wire decoder_1_out0, decoder_1_out1, decoder_1_out2, decoder_1_out3, decoder_1_out4, decoder_1_out5,
       decoder_1_out6, decoder_1_out7, decoder_1_out8, decoder_1_out9, decoder_1_out10, decoder_1_out11,
       decoder_1_out12, decoder_1_out13, decoder_1_out14, decoder_1_out15;
  wire [15:0] a0_q, fp_q, gp_q, multiplexer_1_out, ra_q, s0_q, s1_q, s2_q, s3_q, s4_q, s5_q, sp_q, t1_q,
       t2_q, t3_q, to_q, zero_q;

  Decoder #(.select(4)) decoder_1 (
    .out0(decoder_1_out0), .out1(decoder_1_out1), .out2(decoder_1_out2), .out3(decoder_1_out3),
    .out4(decoder_1_out4), .out5(decoder_1_out5), .out6(decoder_1_out6), .out7(decoder_1_out7),
    .out8(decoder_1_out8), .out9(decoder_1_out9), .out10(decoder_1_out10), .out11(decoder_1_out11),
    .out12(decoder_1_out12), .out13(decoder_1_out13), .out14(decoder_1_out14), .out15(decoder_1_out15),
    .sel(Write_Register));  // open: en
  Multiplexer #(.width(16)) multiplexer_1 (
    .in1(Data), .out(multiplexer_1_out), .sel(Write_register_2));  // open: in0, en
  Register #(.width(16)) zero (.D(multiplexer_1_out), .en(decoder_1_out0), .Q(zero_q), .clk(CLK));  // open: clr
  Register #(.width(16)) to (.D(multiplexer_1_out), .en(decoder_1_out1), .Q(to_q), .clk(CLK));  // open: clr
  Register #(.width(16)) t1 (.D(multiplexer_1_out), .en(decoder_1_out2), .Q(t1_q), .clk(CLK));  // open: clr
  Register #(.width(16)) t2 (.D(multiplexer_1_out), .en(decoder_1_out3), .Q(t2_q), .clk(CLK));  // open: clr
  Register #(.width(16)) t3 (.D(multiplexer_1_out), .en(decoder_1_out4), .Q(t3_q), .clk(CLK));  // open: clr
  Register #(.width(16)) s0 (.D(multiplexer_1_out), .en(decoder_1_out5), .Q(s0_q), .clk(CLK));  // open: clr
  Register #(.width(16)) s1 (.D(multiplexer_1_out), .en(decoder_1_out6), .Q(s1_q), .clk(CLK));  // open: clr
  Register #(.width(16)) s2 (.D(multiplexer_1_out), .en(decoder_1_out7), .Q(s2_q), .clk(CLK));  // open: clr
  Register #(.width(16)) s3 (.D(multiplexer_1_out), .en(decoder_1_out8), .Q(s3_q), .clk(CLK));  // open: clr
  Register #(.width(16)) s4 (.D(multiplexer_1_out), .en(decoder_1_out9), .Q(s4_q), .clk(CLK));  // open: clr
  Register #(.width(16)) s5 (.D(multiplexer_1_out), .en(decoder_1_out10), .Q(s5_q), .clk(CLK));  // open: clr
  Register #(.width(16)) gp (.D(multiplexer_1_out), .en(decoder_1_out11), .Q(gp_q), .clk(CLK));  // open: clr
  Register #(.width(16)) sp (.D(multiplexer_1_out), .en(decoder_1_out12), .Q(sp_q), .clk(CLK));  // open: clr
  Register #(.width(16)) fp (.D(multiplexer_1_out), .en(decoder_1_out13), .Q(fp_q), .clk(CLK));  // open: clr
  Register #(.width(16)) ra (.D(multiplexer_1_out), .en(decoder_1_out14), .Q(ra_q), .clk(CLK));  // open: clr
  Register #(.width(16)) a0 (.D(multiplexer_1_out), .en(decoder_1_out15), .Q(a0_q), .clk(CLK));  // open: clr
  Multiplexer #(.select(4), .width(16)) multiplexer_2 (
    .in0(zero_q), .in1(to_q), .in2(t1_q), .in3(t2_q), .in4(t3_q), .in5(s0_q), .in6(s1_q), .in7(s2_q),
    .in8(s3_q), .in9(s4_q), .in10(s5_q), .in11(gp_q), .in12(sp_q), .in13(fp_q), .in14(ra_q), .in15(a0_q),
    .out(Register_1_Data), .sel(Read_Register_1));  // open: en
  Multiplexer #(.select(4), .width(16)) multiplexer_3 (
    .in0(zero_q), .in1(to_q), .in2(t1_q), .in3(t2_q), .in4(t3_q), .in5(s0_q), .in6(s1_q), .in7(s2_q),
    .in8(s3_q), .in9(s4_q), .in10(s5_q), .in11(gp_q), .in12(sp_q), .in13(fp_q), .in14(ra_q), .in15(a0_q),
    .out(Register_2_Data), .sel(Read_Register_2));  // open: en
endmodule
