// Logisim project 16bit_SLL.circ as structural Verilog: 1 circuit, main circuit main
module main (
  input  [15:0] in_1,
  input  [3:0] SRL,
  output [15:0] out_3
);

  Multiplexer #(.select(4)) multiplexer_1 (
    .in0(in_1[0]), .in1(1'b0), .in2(1'b0), .in3(1'b0), .in4(1'b0), .in5(1'b0), .in6(1'b0), .in7(1'b0),
    .in8(1'b0), .in9(1'b0), .in10(1'b0), .in11(1'b0), .in12(1'b0), .in13(1'b0), .in14(1'b0), .in15(1'b0),
    .out(out_3[0]), .sel(SRL));  // open: en
  Multiplexer #(.select(4)) multiplexer_2 (
    .in0(in_1[1]), .in1(in_1[0]), .in2(1'b0), .in3(1'b0), .in4(1'b0), .in5(1'b0), .in6(1'b0), .in7(1'b0),
    .in8(1'b0), .in9(1'b0), .in10(1'b0), .in11(1'b0), .in12(1'b0), .in13(1'b0), .in14(1'b0), .in15(1'b0),
    .out(out_3[1]), .sel(SRL));  // open: en
  Multiplexer #(.select(4)) multiplexer_3 (
    .in0(in_1[2]), .in1(in_1[1]), .in2(in_1[0]), .in3(1'b0), .in4(1'b0), .in5(1'b0), .in6(1'b0), .in7(1'b0),
    .in8(1'b0), .in9(1'b0), .in10(1'b0), .in11(1'b0), .in12(1'b0), .in13(1'b0), .in14(1'b0), .in15(1'b0),
    .out(out_3[2]), .sel(SRL));  // open: en
  Multiplexer #(.select(4)) multiplexer_4 (
    .in0(in_1[3]), .in1(in_1[2]), .in2(in_1[1]), .in3(in_1[0]), .in4(1'b0), .in5(1'b0), .in6(1'b0),
    .in7(1'b0), .in8(1'b0), .in9(1'b0), .in10(1'b0), .in11(1'b0), .in12(1'b0), .in13(1'b0), .in14(1'b0),
    .in15(1'b0), .out(out_3[3]), .sel(SRL));  // open: en
  Multiplexer #(.select(4)) multiplexer_5 (
    .in0(in_1[4]), .in1(in_1[3]), .in2(in_1[2]), .in3(in_1[1]), .in4(in_1[0]), .in5(1'b0), .in6(1'b0),
    .in7(1'b0), .in8(1'b0), .in9(1'b0), .in10(1'b0), .in11(1'b0), .in12(1'b0), .in13(1'b0), .in14(1'b0),
    .in15(1'b0), .out(out_3[4]), .sel(SRL));  // open: en
  Multiplexer #(.select(4)) multiplexer_6 (
    .in0(in_1[5]), .in1(in_1[4]), .in2(in_1[3]), .in3(in_1[2]), .in4(in_1[1]), .in5(in_1[0]), .in6(1'b0),
    .in7(1'b0), .in8(1'b0), .in9(1'b0), .in10(1'b0), .in11(1'b0), .in12(1'b0), .in13(1'b0), .in14(1'b0),
    .in15(1'b0), .out(out_3[5]), .sel(SRL));  // open: en
  Multiplexer #(.select(4)) multiplexer_7 (
    .in0(in_1[6]), .in1(in_1[5]), .in2(in_1[4]), .in3(in_1[3]), .in4(in_1[2]), .in5(in_1[1]), .in6(in_1[0]),
    .in7(1'b0), .in8(1'b0), .in9(1'b0), .in10(1'b0), .in11(1'b0), .in12(1'b0), .in13(1'b0), .in14(1'b0),
    .in15(1'b0), .out(out_3[6]), .sel(SRL));  // open: en
  Multiplexer #(.select(4)) multiplexer_8 (
    .in0(in_1[7]), .in1(in_1[6]), .in2(in_1[5]), .in3(in_1[4]), .in4(in_1[3]), .in5(in_1[2]), .in6(in_1[1]),
    .in7(in_1[0]), .in8(1'b0), .in9(1'b0), .in10(1'b0), .in11(1'b0), .in12(1'b0), .in13(1'b0), .in14(1'b0),
    .in15(1'b0), .out(out_3[7]), .sel(SRL));  // open: en
  Multiplexer #(.select(4)) multiplexer_9 (
    .in0(in_1[8]), .in1(in_1[7]), .in2(in_1[6]), .in3(in_1[5]), .in4(in_1[4]), .in5(in_1[3]), .in6(in_1[2]),
    .in7(in_1[1]), .in8(in_1[0]), .in9(1'b0), .in10(1'b0), .in11(1'b0), .in12(1'b0), .in13(1'b0),
    .in14(1'b0), .in15(1'b0), .out(out_3[8]), .sel(SRL));  // open: en
  Multiplexer #(.select(4)) multiplexer_10 (
    .in0(in_1[9]), .in1(in_1[8]), .in2(in_1[7]), .in3(in_1[6]), .in4(in_1[5]), .in5(in_1[4]), .in6(in_1[3]),
    .in7(in_1[2]), .in8(in_1[1]), .in9(in_1[0]), .in10(1'b0), .in11(1'b0), .in12(1'b0), .in13(1'b0),
    .in14(1'b0), .in15(1'b0), .out(out_3[9]), .sel(SRL));  // open: en
  Multiplexer #(.select(4)) multiplexer_11 (
    .in0(in_1[10]), .in1(in_1[9]), .in2(in_1[8]), .in3(in_1[7]), .in4(in_1[6]), .in5(in_1[5]), .in6(in_1[4]),
    .in7(in_1[3]), .in8(in_1[2]), .in9(in_1[1]), .in10(in_1[0]), .in11(1'b0), .in12(1'b0), .in13(1'b0),
    .in14(1'b0), .in15(1'b0), .out(out_3[10]), .sel(SRL));  // open: en
  Multiplexer #(.select(4)) multiplexer_12 (
    .in0(in_1[11]), .in1(in_1[10]), .in2(in_1[9]), .in3(in_1[8]), .in4(in_1[7]), .in5(in_1[6]),
    .in6(in_1[5]), .in7(in_1[4]), .in8(in_1[3]), .in9(in_1[2]), .in10(in_1[1]), .in11(in_1[0]), .in12(1'b0),
    .in13(1'b0), .in14(1'b0), .in15(1'b0), .out(out_3[11]), .sel(SRL));  // open: en
  Multiplexer #(.select(4)) multiplexer_13 (
    .in0(in_1[12]), .in1(in_1[11]), .in2(in_1[10]), .in3(in_1[9]), .in4(in_1[8]), .in5(in_1[7]),
    .in6(in_1[6]), .in7(in_1[5]), .in8(in_1[4]), .in9(in_1[3]), .in10(in_1[2]), .in11(in_1[1]),
    .in12(in_1[0]), .in13(1'b0), .in14(1'b0), .in15(1'b0), .out(out_3[12]), .sel(SRL));  // open: en
  Multiplexer #(.select(4)) multiplexer_14 (
    .in0(in_1[13]), .in1(in_1[12]), .in2(in_1[11]), .in3(in_1[10]), .in4(in_1[9]), .in5(in_1[8]),
    .in6(in_1[7]), .in7(in_1[6]), .in8(in_1[5]), .in9(in_1[4]), .in10(in_1[3]), .in11(in_1[2]),
    .in12(in_1[1]), .in13(in_1[0]), .in14(1'b0), .in15(1'b0), .out(out_3[13]), .sel(SRL));  // open: en
  Multiplexer #(.select(4)) multiplexer_15 (
    .in0(in_1[14]), .in1(in_1[13]), .in2(in_1[12]), .in3(in_1[11]), .in4(in_1[10]), .in5(in_1[9]),
    .in6(in_1[8]), .in7(in_1[7]), .in8(in_1[6]), .in9(in_1[5]), .in10(in_1[4]), .in11(in_1[3]),
    .in12(in_1[2]), .in13(in_1[1]), .in14(in_1[0]), .in15(1'b0), .out(out_3[14]), .sel(SRL));  // open: en
  Multiplexer #(.select(4)) multiplexer_16 (
    .in0(in_1[15]), .in1(in_1[14]), .in2(in_1[13]), .in3(in_1[12]), .in4(in_1[11]), .in5(in_1[10]),
    .in6(in_1[9]), .in7(in_1[8]), .in8(in_1[7]), .in9(in_1[6]), .in10(in_1[5]), .in11(in_1[4]),
    .in12(in_1[3]), .in13(in_1[2]), .in14(in_1[1]), .in15(in_1[0]), .out(out_3[15]), .sel(SRL));  // open: en
endmodule
