// Logisim project 16bit_sll_srl.circ as structural Verilog: 1 circuit, main circuit main
module main (
  input  [15:0] in_1,
  input  [3:0] in_2,
  input  in_3,
  output [15:0] out_4
);

  wire [15:0] main_1_out_3, main_2_out_3;

  _16bit_SLL_main main_1 (.in_1(in_1), .SRL(in_2), .out_3(main_1_out_3));
  _16bit_SRL_main main_2 (.in_1(in_1), .ShiftAmt(in_2), .out_3(main_2_out_3));
  Multiplexer #(.width(16)) multiplexer_1 (
    .in0(main_1_out_3), .in1(main_2_out_3), .out(out_4), .sel(in_3));  // open: en
endmodule
